# Fritzing sketch ProjectFzz (saved by Fritzing 0.9.3b)

parts:
  Part1 = Arduino Pro Mini v13
  Part2 = Bluetooth HC-05 Macho
  RHT1 = Humidity and Temperature Sensor RHT03

nets:
  GND: Part1.GND, Part2.GND
  VCC: Part1.VCC, Part2.VCC, RHT1.Vcc
  N1: Part1.D12/MISO, RHT1.Data-signal
  N2: Part1.D11_PWM/MOSI, Part2.RXD
  N3: Part1.D10_PWM/SS, Part2.TXD
